# Fritzing sketch hardware (saved by Fritzing 0.9.5d)
circuit board: 8.46667cm x 5.64444cm
breadboards: 1

parts:
  LED1 = LED - 5mm [color="Red (633nm)" package="5 mm [THT]"]
  Part1 = Arduino Uno (Rev3)
  LED2 = LED - 5mm [color="Yellow (585nm)" package="5 mm [THT]"]
  LED3 = LED - 5mm [color="Green (555nm)" package="5 mm [THT]"]
  S1 = Pushbutton [package="[THT]"]
  S2 = Pushbutton [package="[THT]"]
  S3 = Pushbutton [package="[THT]"]
  J1 = Piezo Speaker
  R1 = Resistor [tolerance=±5% resistance=220 package=THT]
  R2 = Resistor [tolerance=±5% resistance=220 package=THT]
  R3 = Resistor [tolerance=±5% resistance=220 package=THT]
  Part3 = KY-037 High Sensitivity Sound Detection Module [package="Breakout board"]

nets:
  N1: LED1.cathode, Part1.GND, LED2.cathode, LED3.cathode, S1.Pin_3, S1.Pin_4, S2.Pin_3, S2.Pin_4, S3.Pin_3, S3.Pin_4, J1.pin1, Part3.G
  N2: LED1.anode, R1.Pin_0
  N3: Part1.D8, S3.Pin_1, S3.Pin_2
  N4: Part1.D9_PWM, S2.Pin_1, S2.Pin_2
  N5: Part1.D10_PWM/SS, S1.Pin_1, S1.Pin_2
  N6: Part1.D3_PWM, Part3.D0
  N7: Part1.D4, J1.pin2
  N8: Part1.D5_PWM, R3.Pin_1
  N9: Part1.D6_PWM, R2.Pin_1
  N10: Part1.D7, R1.Pin_1
  N11: Part1.5V, Part3.+
  N12: LED2.anode, R2.Pin_0
  N13: LED3.anode, R3.Pin_0

custom parts:
  KY-037 High Sensitivity Sound Detection Module: KY-037 high sensitivity sound detection module is an analog/digital sensor that uses a condenser microphone to observe changes in environment noise.
